// Logisim project Sap1.circ as structural Verilog: 13 circuits, main circuit IR
module main (
  input  Ea,
  input  Cp,
  input  in_3,
  input  La,
  input  CLR,
  input  Ep,
  input  Su,
  input  Lm,
  input  Eu,
  input  Lb,
  input  Lo,
  input  CE,
  input  Li,
  input  Ei,
  output [3:0] out_15,
  output [3:0] out_16,
  output [7:0] out_17
);

  wire CLK_out, ir_1_h0, ir_1_h1, ir_1_h2, ir_1_h3, not_1_out;
  wire [3:0] mar_1_q0, Output_out, Output_out_2;
  wire [7:0] B_out;

  Clock CLK (.out(CLK_out));
  not not_1 (not_1_out, CLR);
  PC pc_1 (
    .Cp(Cp), .CLK(CLK_out), .CLR(not_1_out), .Ep(Ep), .Q0(out_16[0]), .Q1(out_16[1]), .Q2(out_16[2]),
    .Q3(out_16[3]));
  MAR mar_1 (
    .CLK(CLK_out), .Lm(Lm), .Q3(mar_1_q0[3]), .Q2(mar_1_q0[2]), .Q1(mar_1_q0[1]), .Q0(mar_1_q0[0]),
    .in_2(out_16[0]), .in_3(out_16[1]), .in_6(out_16[2]), .in_7(out_16[3]));  // open: CLR
  IR ir_1 (
    .Li(Li), .CLK(CLK_out), .CLR(CLR), .Ei(Ei), .h3(ir_1_h3), .h2(ir_1_h2), .h1(ir_1_h1), .h0(ir_1_h0),
    .high(out_15), .low(out_16), .C9out(out_16));
  control_matrix control_matrix_1 (
    .in_1(ir_1_h3), .in_2(ir_1_h2), .in_3(ir_1_h1), .in_4(ir_1_h0));  // open: CLK, CLR, out_8, Cp, Ep, Lm, CE, Li, Ei, La, Ea, Su, Eu, Lb, Lo, in_6
  RAM #(.addrWidth(4)) ram_1 (.addr(mar_1_q0), .data({out_15, out_16}), .sel(CE));  // open: clk, ld, clr
  Hex_Digit_Display hex_digit_display_1 (.value(Output_out_2));  // open: dp
  ACC acc_1 (
    .La(La), .CLK(CLK_out), .CLR(in_3), .Ea(Ea), .high(out_15), .low(out_16), .OUT(out_17),
    .OUT2({out_15, out_16}));
  ADD_SUB add_sub_1 (.OUT({out_15, out_16}), .A(out_17), .B(B_out), .Su(Su), .Eu(Eu));
  B_reg B (.IN({out_15, out_16}), .OUT(B_out), .Lb(Lb), .CLK(CLK_out));
  B_reg Output (.IN({out_15, out_16}), .OUT({Output_out_2, Output_out}), .Lb(Lo), .CLK(CLK_out));
  Hex_Digit_Display hex_digit_display_2 (.value(Output_out));  // open: dp
endmodule

module PC (
  input  Cp,
  input  CLK,
  input  CLR,
  input  Ep,
  output Q0,
  output Q1,
  output Q2,
  output Q3
);

  wire not_1_out, not_2_out, not_3_out, Q0_q, Q1_q, Q2_q, Q3_q;

  not not_1 (not_1_out, Q2_q);
  assign Q3 = Ep ? Q3_q : 1'bz;  // Controlled_Buffer controlled_buffer_1
  J_K_Flip_Flop u_Q3 (.J(Cp), .clk(not_1_out), .K(Cp), .Q(Q3_q), .reset(CLR));  // open: Qn, preset, en
  J_K_Flip_Flop u_Q2 (.J(Cp), .clk(not_2_out), .K(Cp), .Q(Q2_q), .reset(CLR));  // open: Qn, preset, en
  not not_2 (not_2_out, Q1_q);
  assign Q2 = Ep ? Q2_q : 1'bz;  // Controlled_Buffer controlled_buffer_2
  not not_3 (not_3_out, Q0_q);
  J_K_Flip_Flop u_Q1 (.J(Cp), .clk(not_3_out), .K(Cp), .Q(Q1_q), .reset(CLR));  // open: Qn, preset, en
  assign Q1 = Ep ? Q1_q : 1'bz;  // Controlled_Buffer controlled_buffer_3
  J_K_Flip_Flop u_Q0 (.J(Cp), .clk(CLK), .K(Cp), .Q(Q0_q), .reset(CLR));  // open: Qn, preset, en
  assign Q0 = Ep ? Q0_q : 1'bz;  // Controlled_Buffer controlled_buffer_4
endmodule

module MAR (
  input  Lm,
  input  in_2,
  input  in_3,
  input  CLK,
  input  CLR,
  input  in_6,
  input  in_7,
  output Q3,
  output Q2,
  output Q1,
  output Q0
);

  wire and_1_out, and_2_out, and_3_out, and_4_out, and_5_out, and_6_out, and_7_out, and_8_out, not_1_out,
       or_1_out, or_2_out, or_3_out, or_4_out;

  Register #(.width(1)) register_1 (.D(or_1_out), .en(1'b1), .Q(Q0), .clk(CLK), .clr(CLR));
  Register #(.width(1)) register_2 (.D(or_2_out), .en(1'b1), .Q(Q1), .clk(CLK), .clr(CLR));
  Register #(.width(1)) register_3 (.D(or_3_out), .en(1'b1), .Q(Q2), .clk(CLK), .clr(CLR));
  Register #(.width(1)) register_4 (.D(or_4_out), .en(1'b1), .Q(Q3), .clk(CLK), .clr(CLR));
  or or_1 (or_1_out, and_1_out, and_2_out);
  or or_2 (or_2_out, and_3_out, and_4_out);
  or or_3 (or_3_out, and_5_out, and_6_out);
  or or_4 (or_4_out, and_7_out, and_8_out);
  and and_1 (and_1_out, Lm, in_2);
  and and_2 (and_2_out, not_1_out, Q0);
  and and_3 (and_3_out, in_3, Lm);
  and and_4 (and_4_out, not_1_out, Q1);
  and and_5 (and_5_out, in_6, Lm);
  and and_6 (and_6_out, not_1_out, Q2);
  and and_7 (and_7_out, in_7, Lm);
  and and_8 (and_8_out, not_1_out, Q3);
  not not_1 (not_1_out, Lm);
endmodule

module IR (
  input  [3:0] high,
  input  [3:0] low,
  input  Li,
  input  CLK,
  input  CLR,
  input  Ei,
  output [3:0] C9out,
  output h3,
  output h2,
  output h1,
  output h0
);

  wire C9_q0, C9_q1, C9_q2, C9_q3;

  Mar2 C8 (
    .CLK(CLK), .CLR(CLR), .Lm(Li), .Q3(h3), .Q2(h2), .Q1(h1), .Q0(h0), .in_2(high[0]), .in_3(high[1]),
    .in_5(high[2]), .in_7(high[3]));
  Mar2 C9 (
    .CLK(CLK), .CLR(CLR), .Lm(Li), .Q3(C9_q3), .Q2(C9_q2), .Q1(C9_q1), .Q0(C9_q0), .in_2(low[0]),
    .in_3(low[1]), .in_5(low[2]), .in_7(low[3]));
  assign C9out[2] = Ei ? C9_q2 : 1'bz;  // Controlled_Buffer controlled_buffer_1
  assign C9out[3] = Ei ? C9_q3 : 1'bz;  // Controlled_Buffer controlled_buffer_2
  assign C9out[0] = Ei ? C9_q0 : 1'bz;  // Controlled_Buffer controlled_buffer_3
  assign C9out[1] = Ei ? C9_q1 : 1'bz;  // Controlled_Buffer controlled_buffer_4
endmodule

module Mar2 (
  input  Lm,
  input  in_2,
  input  in_3,
  input  CLK,
  input  in_5,
  input  CLR,
  input  in_7,
  output Q3,
  output Q2,
  output Q1,
  output Q0
);

  wire and_1_out, and_2_out, and_3_out, and_4_out, and_5_out, and_6_out, and_7_out, and_8_out, not_1_out,
       or_1_out, or_2_out, or_3_out, or_4_out;

  Register #(.width(1)) register_1 (.D(or_1_out), .en(1'b1), .Q(Q0), .clk(CLK), .clr(CLR));
  Register #(.width(1)) register_2 (.D(or_2_out), .en(1'b1), .Q(Q1), .clk(CLK), .clr(CLR));
  Register #(.width(1)) register_3 (.D(or_3_out), .en(1'b1), .Q(Q2), .clk(CLK), .clr(CLR));
  Register #(.width(1)) register_4 (.D(or_4_out), .en(1'b1), .Q(Q3), .clk(CLK), .clr(CLR));
  or or_1 (or_1_out, and_1_out, and_2_out);
  or or_2 (or_2_out, and_3_out, and_4_out);
  or or_3 (or_3_out, and_5_out, and_6_out);
  or or_4 (or_4_out, and_7_out, and_8_out);
  and and_1 (and_1_out, Lm, in_2);
  and and_2 (and_2_out, not_1_out, Q0);
  and and_3 (and_3_out, in_3, Lm);
  and and_4 (and_4_out, not_1_out, Q1);
  and and_5 (and_5_out, in_5, Lm);
  and and_6 (and_6_out, not_1_out, Q2);
  and and_7 (and_7_out, in_7, Lm);
  and and_8 (and_8_out, not_1_out, Q3);
  not not_1 (not_1_out, Lm);
endmodule

module ACC (
  input  [3:0] high,
  input  [3:0] low,
  input  La,
  input  CLK,
  input  CLR,
  input  Ea,
  output [7:0] OUT,
  output [7:0] OUT2
);

  Mar2 C8 (
    .CLK(CLK), .CLR(CLR), .Lm(La), .Q3(OUT[7]), .Q2(OUT[6]), .Q1(OUT[5]), .Q0(OUT[4]), .in_2(high[0]),
    .in_3(high[1]), .in_5(high[2]), .in_7(high[3]));
  Mar2 C9 (
    .CLK(CLK), .CLR(CLR), .Lm(La), .Q3(OUT[3]), .Q2(OUT[2]), .Q1(OUT[1]), .Q0(OUT[0]), .in_2(low[0]),
    .in_3(low[1]), .in_5(low[2]), .in_7(low[3]));
  assign OUT2 = Ea ? OUT : 8'bz;  // Controlled_Buffer controlled_buffer_1
endmodule

// A/S
module ADD_SUB (
  input  Su,
  input  [7:0] A,
  input  Eu,
  input  [7:0] B,
  output [7:0] OUT
);

  wire [7:0] adder_1_out, xor_8_out;

  xor xor_1 (xor_8_out[7], B[7], Su);
  xor xor_2 (xor_8_out[6], B[6], Su);
  xor xor_3 (xor_8_out[5], B[5], Su);
  assign OUT = Eu ? adder_1_out : 8'bz;  // Controlled_Buffer controlled_buffer_1
  Adder adder_1 (.a(A), .b(xor_8_out), .out(adder_1_out), .cin(Su));  // open: cout
  xor xor_4 (xor_8_out[4], B[4], Su);
  xor xor_5 (xor_8_out[3], B[3], Su);
  xor xor_6 (xor_8_out[1], B[1], Su);
  xor xor_7 (xor_8_out[2], B[2], Su);
  xor xor_8 (xor_8_out[0], B[0], Su);
endmodule

module B_reg (
  input  Lb,
  input  [7:0] IN,
  input  CLK,
  output [7:0] OUT
);

  wire [7:0] and_1_out;

  assign and_1_out = {8{Lb}} & IN;  // AND_Gate and_1, 8 bits wide
  Register register_1 (.D(and_1_out), .Q(OUT), .clk(CLK));  // open: en, clr
endmodule

module Ring_counter (
  input  Preset,
  input  CLK,
  input  CLR,
  output out_4,
  output out_5,
  output out_6,
  output out_7,
  output out_8,
  output out_9
);

  D_Flip_Flop d_ff_1 (.clk(CLK), .D(out_4), .Q(out_9), .preset(CLR), .reset(Preset));  // open: Qn, en
  D_Flip_Flop d_ff_2 (.clk(CLK), .D(out_9), .Q(out_8), .preset(Preset), .reset(CLR));  // open: Qn, en
  D_Flip_Flop d_ff_3 (.clk(CLK), .D(out_8), .Q(out_7), .preset(Preset), .reset(CLR));  // open: Qn, en
  D_Flip_Flop d_ff_4 (.clk(CLK), .D(out_7), .Q(out_6), .preset(Preset), .reset(CLR));  // open: Qn, en
  D_Flip_Flop d_ff_5 (.clk(CLK), .D(out_6), .Q(out_5), .preset(Preset), .reset(CLR));  // open: Qn, en
  D_Flip_Flop d_ff_6 (.clk(CLK), .D(out_5), .Q(out_4), .preset(Preset), .reset(CLR));  // open: Qn, en
endmodule

module control_matrix (
  input  in_1,
  input  in_2,
  input  in_3,
  input  in_4,
  input  CLK,
  input  in_6,
  input  CLR,
  output out_8,
  output Cp,
  output Ep,
  output CE,
  output Li,
  output Ea,
  output Su,
  output Eu,
  output Lb,
  output Lo,
  output Ei,
  output La,
  output Lm
);

  wire and_1_out, and_2_out, and_3_out, and_4_out, and_5_out, and_6_out, and_7_out, and_8_out, and_9_out,
       and_10_out, and_11_out, and_12_out, and_15_out, and_16_out, and_17_out, and_18_out, and_19_out,
       buffer_1_out, buffer_2_out, instruction_decoder_1_add, instruction_decoder_1_lda,
       instruction_decoder_1_out, instruction_decoder_1_sub, or_1_out, or_2_out, or_3_out, or_4_out,
       or_6_out, ring_counter_1_out_4, ring_counter_1_out_5, ring_counter_1_out_6, ring_counter_1_out_7;

  instruction_decoder instruction_decoder_1 (
    .HLT(out_8), .in_1(in_1), .in_2(in_2), .in_3(in_3), .in_4(in_4), .LDA(instruction_decoder_1_lda),
    .ADD(instruction_decoder_1_add), .SUB(instruction_decoder_1_sub), .Out(instruction_decoder_1_out));
  buf buffer_1 (buffer_1_out, Ep);
  and and_1 (and_1_out, instruction_decoder_1_add, ring_counter_1_out_6);
  and and_2 (and_2_out, instruction_decoder_1_lda, ring_counter_1_out_6);
  or or_1 (or_1_out, buffer_1_out, and_2_out, and_1_out, and_3_out);
  not not_1 (Lm, or_1_out);
  buf buffer_2 (buffer_2_out, ring_counter_1_out_7);
  and and_3 (and_3_out, instruction_decoder_1_sub, ring_counter_1_out_6);
  Ring_counter ring_counter_1 (
    .CLK(CLK), .CLR(CLR), .out_4(ring_counter_1_out_4), .out_5(ring_counter_1_out_5),
    .out_6(ring_counter_1_out_6), .out_7(ring_counter_1_out_7), .out_8(Cp), .out_9(Ep), .Preset(in_6));
  and and_4 (and_4_out, instruction_decoder_1_lda, ring_counter_1_out_5);
  or or_2 (or_2_out, buffer_2_out, and_4_out, and_6_out, and_5_out);
  not not_2 (CE, or_2_out);
  and and_5 (and_5_out, instruction_decoder_1_sub, ring_counter_1_out_5);
  and and_6 (and_6_out, instruction_decoder_1_add, ring_counter_1_out_5);
  and and_7 (and_7_out, instruction_decoder_1_lda, ring_counter_1_out_6);
  or or_3 (or_3_out, and_7_out, and_9_out, and_8_out);
  not not_3 (Li, ring_counter_1_out_7);
  not not_4 (Ei, or_3_out);
  and and_8 (and_8_out, instruction_decoder_1_sub, ring_counter_1_out_6);
  and and_9 (and_9_out, instruction_decoder_1_add, ring_counter_1_out_6);
  and and_10 (and_10_out, instruction_decoder_1_lda, ring_counter_1_out_5);
  or or_4 (or_4_out, and_10_out, and_11_out, and_12_out);
  not not_5 (La, or_4_out);
  and and_11 (and_11_out, instruction_decoder_1_add, ring_counter_1_out_4);
  and and_12 (and_12_out, instruction_decoder_1_sub, ring_counter_1_out_4);
  and and_13 (Su, instruction_decoder_1_sub, ring_counter_1_out_4);
  and and_14 (Ea, instruction_decoder_1_out, ring_counter_1_out_6);
  and and_15 (and_15_out, instruction_decoder_1_add, ring_counter_1_out_4);
  or or_5 (Eu, and_15_out, and_17_out);
  and and_16 (and_16_out, instruction_decoder_1_add, ring_counter_1_out_5);
  and and_17 (and_17_out, instruction_decoder_1_sub, ring_counter_1_out_4);
  and and_18 (and_18_out, instruction_decoder_1_sub, ring_counter_1_out_5);
  or or_6 (or_6_out, and_16_out, and_18_out);
  not not_6 (Lb, or_6_out);
  and and_19 (and_19_out, instruction_decoder_1_out, ring_counter_1_out_6);
  not not_7 (Lo, and_19_out);
endmodule

module instruction_decoder (
  input  in_1,
  input  in_2,
  input  in_3,
  input  in_4,
  output HLT,
  output ADD,
  output SUB,
  output Out,
  output LDA
);

  wire not_1_out, not_2_out, not_3_out, not_4_out;

  not not_1 (not_1_out, in_1);
  not not_2 (not_2_out, in_2);
  not not_3 (not_3_out, in_3);
  not not_4 (not_4_out, in_4);
  and and_1 (LDA, not_1_out, not_2_out, not_3_out, not_4_out);
  and and_2 (ADD, not_1_out, not_2_out, not_3_out, in_4);
  and and_3 (SUB, not_1_out, not_2_out, in_3, not_4_out);
  and and_4 (Out, in_1, in_2, in_3, not_4_out);
  and and_5 (HLT, in_1, in_2, in_3, in_4);
endmodule

module extra (
  input  Ea,
  input  Cp,
  input  in_3,
  input  La,
  input  CLR,
  input  Ep,
  input  Su,
  input  Lm,
  input  Eu,
  input  Lb,
  input  Lo,
  input  CE,
  input  Li,
  input  Ei,
  input  in_15,
  output [3:0] out_16,
  output [3:0] out_17,
  output [7:0] out_18
);

  wire CLK_out, con_extra_1_ce, con_extra_1_cp, con_extra_1_ea, con_extra_1_ei, con_extra_1_ep,
       con_extra_1_eu, con_extra_1_la, con_extra_1_lb, con_extra_1_li, con_extra_1_lm, con_extra_1_lo,
       con_extra_1_out_8, con_extra_1_su, controlled_buffer_1_out, ir_1_h0, ir_1_h1, ir_1_h2, ir_1_h3,
       not_1_out;
  wire [3:0] mar_1_q0, Output_out, Output_out_2;
  wire [7:0] B_out;

  Clock CLK (.out(CLK_out));
  not not_1 (not_1_out, con_extra_1_out_8);
  assign controlled_buffer_1_out = not_1_out ? CLK_out : 1'bz;  // Controlled_Buffer controlled_buffer_1
  PC pc_1 (
    .Cp(con_extra_1_cp), .CLK(controlled_buffer_1_out), .CLR(CLR), .Ep(con_extra_1_ep), .Q0(out_17[0]),
    .Q1(out_17[1]), .Q2(out_17[2]), .Q3(out_17[3]));
  MAR mar_1 (
    .CLK(controlled_buffer_1_out), .Lm(con_extra_1_lm), .Q3(mar_1_q0[3]), .Q2(mar_1_q0[2]), .Q1(mar_1_q0[1]),
    .Q0(mar_1_q0[0]), .in_2(out_17[0]), .in_3(out_17[1]), .in_6(out_17[2]), .in_7(out_17[3]));  // open: CLR
  IR ir_1 (
    .Li(con_extra_1_li), .CLK(controlled_buffer_1_out), .CLR(CLR), .Ei(con_extra_1_ei), .h3(ir_1_h3),
    .h2(ir_1_h2), .h1(ir_1_h1), .h0(ir_1_h0), .high(out_16), .low(out_17), .C9out(out_17));
  con_extra con_extra_1 (
    .CLK(controlled_buffer_1_out), .CLR(CLR), .out_8(con_extra_1_out_8), .in_1(ir_1_h3), .in_2(ir_1_h2),
    .in_3(ir_1_h1), .in_4(ir_1_h0), .Cp(con_extra_1_cp), .Ep(con_extra_1_ep), .Lm(con_extra_1_lm),
    .CE(con_extra_1_ce), .Li(con_extra_1_li), .Ei(con_extra_1_ei), .La(con_extra_1_la), .Ea(con_extra_1_ea),
    .Su(con_extra_1_su), .Eu(con_extra_1_eu), .Lb(con_extra_1_lb), .Lo(con_extra_1_lo), .in_6(in_15));
  RAM #(.addrWidth(4)) ram_1 (.addr(mar_1_q0), .data({out_16, out_17}), .sel(con_extra_1_ce));  // open: clk, ld, clr
  Hex_Digit_Display hex_digit_display_1 (.value(Output_out_2));  // open: dp
  ACC acc_1 (
    .La(con_extra_1_la), .CLK(controlled_buffer_1_out), .CLR(in_3), .Ea(con_extra_1_ea), .high(out_16),
    .low(out_17), .OUT(out_18), .OUT2({out_16, out_17}));
  ADD_SUB add_sub_1 (.OUT({out_16, out_17}), .A(out_18), .B(B_out), .Su(con_extra_1_su), .Eu(con_extra_1_eu));
  B_reg B (.IN({out_16, out_17}), .OUT(B_out), .Lb(con_extra_1_lb), .CLK(controlled_buffer_1_out));
  B_reg Output (
    .IN({out_16, out_17}), .OUT({Output_out_2, Output_out}), .Lb(con_extra_1_lo),
    .CLK(controlled_buffer_1_out));
  Hex_Digit_Display hex_digit_display_2 (.value(Output_out));  // open: dp
endmodule

module con_extra (
  input  in_1,
  input  in_2,
  input  in_3,
  input  in_4,
  input  CLK,
  input  in_6,
  input  CLR,
  output out_8,
  output Cp,
  output Ep,
  output CE,
  output Li,
  output Ea,
  output Su,
  output Eu,
  output Lb,
  output Lo,
  output Ei,
  output La,
  output Lm
);

  wire and_1_out, and_2_out, and_3_out, and_4_out, and_5_out, and_6_out, and_7_out, and_8_out, and_9_out,
       and_10_out, and_11_out, and_12_out, and_15_out, and_16_out, and_17_out, and_18_out, buffer_1_out,
       buffer_2_out, instruction_decoder_1_add, instruction_decoder_1_lda, instruction_decoder_1_out,
       instruction_decoder_1_sub, ring_counter_1_out_4, ring_counter_1_out_5, ring_counter_1_out_6;

  instruction_decoder instruction_decoder_1 (
    .HLT(out_8), .in_1(in_1), .in_2(in_2), .in_3(in_3), .in_4(in_4), .LDA(instruction_decoder_1_lda),
    .ADD(instruction_decoder_1_add), .SUB(instruction_decoder_1_sub), .Out(instruction_decoder_1_out));
  buf buffer_1 (buffer_1_out, Ep);
  and and_1 (and_1_out, instruction_decoder_1_add, ring_counter_1_out_6);
  and and_2 (and_2_out, instruction_decoder_1_lda, ring_counter_1_out_6);
  or or_1 (Lm, buffer_1_out, and_2_out, and_1_out, and_3_out);
  and and_3 (and_3_out, instruction_decoder_1_sub, ring_counter_1_out_6);
  Ring_counter ring_counter_1 (
    .CLK(CLK), .CLR(CLR), .out_4(ring_counter_1_out_4), .out_5(ring_counter_1_out_5),
    .out_6(ring_counter_1_out_6), .out_7(Li), .out_8(Cp), .out_9(Ep), .Preset(in_6));
  buf buffer_2 (buffer_2_out, Li);
  and and_4 (and_4_out, instruction_decoder_1_lda, ring_counter_1_out_5);
  and and_5 (and_5_out, instruction_decoder_1_sub, ring_counter_1_out_5);
  and and_6 (and_6_out, instruction_decoder_1_add, ring_counter_1_out_5);
  or or_2 (CE, buffer_2_out, and_4_out, and_6_out, and_5_out);
  and and_7 (and_7_out, instruction_decoder_1_lda, ring_counter_1_out_6);
  and and_8 (and_8_out, instruction_decoder_1_add, ring_counter_1_out_6);
  and and_9 (and_9_out, instruction_decoder_1_sub, ring_counter_1_out_6);
  or or_3 (Ei, and_7_out, and_8_out, and_9_out);
  and and_10 (and_10_out, instruction_decoder_1_lda, ring_counter_1_out_5);
  and and_11 (and_11_out, instruction_decoder_1_add, ring_counter_1_out_4);
  and and_12 (and_12_out, instruction_decoder_1_sub, ring_counter_1_out_4);
  or or_4 (La, and_10_out, and_11_out, and_12_out);
  and and_13 (Ea, instruction_decoder_1_out, ring_counter_1_out_6);
  and and_14 (Su, instruction_decoder_1_sub, ring_counter_1_out_4);
  and and_15 (and_15_out, instruction_decoder_1_add, ring_counter_1_out_4);
  or or_5 (Eu, and_15_out, and_16_out);
  and and_16 (and_16_out, instruction_decoder_1_sub, ring_counter_1_out_4);
  and and_17 (and_17_out, instruction_decoder_1_sub, ring_counter_1_out_5);
  and and_18 (and_18_out, instruction_decoder_1_add, ring_counter_1_out_5);
  or or_6 (Lb, and_18_out, and_17_out);
  nand nand_1 (Lo, instruction_decoder_1_out, ring_counter_1_out_6);
endmodule
